// Logisim project halfAdder.circ as structural Verilog: 14 circuits, main circuit main
module main (
  input  a0,
  input  a1,
  input  a2,
  input  a3,
  input  a4,
  input  a5,
  input  a6,
  input  a7,
  input  b0,
  input  b1,
  input  b2,
  input  b3,
  input  b4,
  input  b5,
  input  b6,
  input  b7,
  input  s0,
  input  s1,
  input  s2,
  output out_20,
  output out_21,
  output out_22,
  output out_23,
  output out_24,
  output out_25,
  output out_26,
  output out_27
);

  wire [7:0] \Adição , \Divisão , \Multipicação , \Multiplicação , Resto, \Subtração ;

  Adder_8_bits adder_8_bits_1 (
    .r0(\Adição [0]), .r1(\Adição [1]), .r2(\Adição [2]), .r3(\Adição [3]), .r4(\Adição [4]),
    .r5(\Adição [5]), .r6(\Adição [6]), .r7(\Adição [7]), .b0(b0), .b1(b1), .b2(b2), .b3(b3), .b4(b4),
    .b5(b5), .b6(b6), .b7(b7), .a0(a0), .a1(a1), .a2(a2), .a3(a3), .a4(a4), .a5(a5), .a6(a6), .a7(a7));  // open: Overflow
  Subtraction subtraction_1 (
    .a0(a0), .a1(a1), .a2(a2), .a3(a3), .a4(a4), .a5(a5), .a6(a6), .a7(a7), .b0(b0), .b1(b1), .b2(b2),
    .b3(b3), .b4(b4), .b5(b5), .b6(b6), .b7(b7), .r0(\Subtração [0]), .r1(\Subtração [1]),
    .r2(\Subtração [2]), .r3(\Subtração [3]), .r4(\Subtração [4]), .r5(\Subtração [5]), .r6(\Subtração [6]),
    .r7(\Subtração [7]));  // open: Overflow
  Resto resto_1 (
    .a0(a0), .a1(a1), .a2(a2), .a3(a3), .a4(a4), .a5(a5), .a6(a6), .a7(a7), .b0(b0), .b1(b1), .b2(b2),
    .b3(b3), .b4(b4), .b5(b5), .b6(b6), .b7(b7), .out_17(Resto[0]), .out_18(Resto[1]), .out_19(Resto[2]),
    .out_20(Resto[3]), .out_21(Resto[4]), .out_22(Resto[5]), .out_23(Resto[6]), .out_24(Resto[7]));
  Megaboga_Multiplier megaboga_multiplier_1 (
    .a0(a0), .a1(a1), .a2(a2), .a3(a3), .a4(a4), .a5(a5), .a6(a6), .a7(a7), .b0(b0), .b1(b1), .b2(b2),
    .b3(b3), .b4(b4), .b5(b5), .b6(b6), .b7(b7), .out_17(\Multiplicação [0]), .out_18(\Multiplicação [1]),
    .out_19(\Multiplicação [2]), .out_20(\Multiplicação [3]), .out_21(\Multiplicação [4]),
    .out_22(\Multiplicação [5]), .out_23(\Multiplicação [6]), .out_24(\Multiplicação [7]));
  \Divisão  \divisão_1  (
    .DIVIDENDO(a0), .in_2(a1), .in_3(a2), .in_4(a3), .in_5(a4), .in_6(a5), .in_7(a6), .in_8(a7), .in_9(b0),
    .in_10(b1), .in_11(b2), .in_12(b3), .in_13(b4), .in_14(b5), .in_15(b6), .in_16(b7),
    .out_17(\Divisão [0]), .out_18(\Divisão [1]), .out_19(\Divisão [2]), .out_20(\Divisão [3]),
    .out_21(\Divisão [4]), .out_22(\Divisão [5]), .out_23(\Divisão [6]), .out_24(\Divisão [7]));
  Multiplexer #(.select(3), .width(8)) multiplexer_1 (
    .in0(\Adição ), .in1(\Subtração ), .in2(\Multipicação ), .in3(\Divisão ), .in4(Resto),
    .out({out_27, out_26, out_25, out_24, out_23, out_22, out_21, out_20}), .sel({s2, s1, s0}), .en(1'b1));  // open: in5, in6, in7

  // Other names for the same wires on the sheet: Result[7:0] = {out_27, out_26, out_25, out_24, out_23, out_22, out_21, out_20}
endmodule

module half_Adder (
  input  a,
  input  b,
  output Carry,
  output Out
);

  and and_1 (Carry, a, b);
  xor xor_1 (Out, a, b);
endmodule

module Full_Adder (
  input  Carry_in,
  input  a_in,
  input  b_in,
  output Result,
  output Carry
);

  wire half_adder_1_carry, half_adder_1_out, half_adder_2_carry;

  half_Adder half_adder_1 (.a(a_in), .b(b_in), .Carry(half_adder_1_carry), .Out(half_adder_1_out));
  half_Adder half_adder_2 (.a(Carry_in), .b(half_adder_1_out), .Carry(half_adder_2_carry), .Out(Result));
  or or_1 (Carry, half_adder_2_carry, half_adder_1_carry);
endmodule

module Adder_8_bits (
  input  a0,
  input  a1,
  input  a2,
  input  a3,
  input  a4,
  input  a5,
  input  a6,
  input  a7,
  input  b0,
  input  b1,
  input  b2,
  input  b3,
  input  b4,
  input  b5,
  input  b6,
  input  b7,
  output r0,
  output r1,
  output r2,
  output r3,
  output r4,
  output r5,
  output r6,
  output r7,
  output Overflow
);

  wire and_1_out, and_2_out, and_3_out, and_4_out, full_adder_1_carry, full_adder_2_carry,
       full_adder_3_carry, full_adder_4_carry, full_adder_5_carry, full_adder_6_carry, full_adder_7_carry,
       not_1_out, not_2_out, not_3_out;

  Full_Adder full_adder_1 (.Carry_in(1'b0), .a_in(a0), .b_in(b0), .Result(r0), .Carry(full_adder_1_carry));
  Full_Adder full_adder_2 (
    .Carry_in(full_adder_1_carry), .a_in(a1), .b_in(b1), .Result(r1), .Carry(full_adder_2_carry));
  Full_Adder full_adder_3 (
    .Carry_in(full_adder_2_carry), .a_in(a2), .b_in(b2), .Result(r2), .Carry(full_adder_3_carry));
  Full_Adder full_adder_4 (
    .Carry_in(full_adder_3_carry), .a_in(a3), .b_in(b3), .Result(r3), .Carry(full_adder_4_carry));
  Full_Adder full_adder_5 (
    .Carry_in(full_adder_4_carry), .a_in(a4), .b_in(b4), .Result(r4), .Carry(full_adder_5_carry));
  Full_Adder full_adder_6 (
    .Carry_in(full_adder_5_carry), .a_in(a5), .b_in(b5), .Result(r5), .Carry(full_adder_6_carry));
  Full_Adder full_adder_7 (
    .Carry_in(full_adder_6_carry), .a_in(a6), .b_in(b6), .Result(r6), .Carry(full_adder_7_carry));
  Full_Adder full_adder_8 (.Carry_in(full_adder_7_carry), .a_in(a7), .b_in(b7), .Result(r7));  // open: Carry
  not not_1 (not_1_out, a7);
  not not_2 (not_2_out, b7);
  and and_1 (and_1_out, a7, b7);
  not not_3 (not_3_out, r7);
  and and_2 (and_2_out, not_1_out, not_2_out);
  and and_3 (and_3_out, and_1_out, not_3_out);
  and and_4 (and_4_out, and_2_out, r7);
  or or_1 (Overflow, and_4_out, and_3_out);

  // Notes on the sheet:
  //   Const 0
endmodule

module Two_s_complement (
  input  in_1,
  input  in_2,
  input  in_3,
  input  in_4,
  input  in_5,
  input  in_6,
  input  in_7,
  input  in_8,
  output out_9,
  output out_10,
  output out_11,
  output out_12,
  output out_13,
  output out_14,
  output out_15,
  output out_16,
  output out_17
);

  wire not_1_out, not_2_out, not_3_out, not_4_out, not_5_out, not_6_out, not_7_out, not_8_out;

  not not_1 (not_1_out, in_1);
  not not_2 (not_2_out, in_2);
  not not_3 (not_3_out, in_3);
  not not_4 (not_4_out, in_4);
  not not_5 (not_5_out, in_5);
  not not_6 (not_6_out, in_6);
  not not_7 (not_7_out, in_7);
  not not_8 (not_8_out, in_8);
  Adder_8_bits adder_8_bits_1 (
    .r0(out_9), .r1(out_10), .r2(out_11), .r3(out_12), .r4(out_13), .r5(out_14), .r6(out_15), .r7(out_16),
    .b0(1'b1), .b1(1'b0), .b2(1'b0), .b3(1'b0), .b4(1'b0), .b5(1'b0), .b6(1'b0), .b7(1'b0), .a0(not_1_out),
    .a1(not_2_out), .a2(not_3_out), .a3(not_4_out), .a4(not_5_out), .a5(not_6_out), .a6(not_7_out),
    .a7(not_8_out), .Overflow(out_17));
endmodule

module Subtraction (
  input  a0,
  input  a1,
  input  a2,
  input  a3,
  input  a4,
  input  a5,
  input  a6,
  input  a7,
  input  b0,
  input  b1,
  input  b2,
  input  b3,
  input  b4,
  input  b5,
  input  b6,
  input  b7,
  output r0,
  output r1,
  output r2,
  output r3,
  output r4,
  output r5,
  output r6,
  output r7,
  output Overflow
);

  wire full_adder_1_carry, full_adder_2_carry, full_adder_3_carry, full_adder_4_carry, full_adder_5_carry,
       full_adder_6_carry, full_adder_7_carry, two_s_complement_1_out_9, two_s_complement_1_out_10,
       two_s_complement_1_out_11, two_s_complement_1_out_12, two_s_complement_1_out_13,
       two_s_complement_1_out_14, two_s_complement_1_out_15, two_s_complement_1_out_16;

  Two_s_complement two_s_complement_1 (
    .in_1(b0), .in_2(b1), .in_3(b2), .in_4(b3), .in_5(b4), .in_6(b5), .in_7(b6), .in_8(b7),
    .out_9(two_s_complement_1_out_9), .out_10(two_s_complement_1_out_10), .out_11(two_s_complement_1_out_11),
    .out_12(two_s_complement_1_out_12), .out_13(two_s_complement_1_out_13),
    .out_14(two_s_complement_1_out_14), .out_15(two_s_complement_1_out_15), .out_16(two_s_complement_1_out_16));  // open: out_17
  Full_Adder full_adder_1 (
    .Carry_in(1'b0), .a_in(a0), .b_in(two_s_complement_1_out_9), .Result(r0), .Carry(full_adder_1_carry));
  Full_Adder full_adder_2 (
    .Carry_in(full_adder_1_carry), .a_in(a1), .b_in(two_s_complement_1_out_10), .Result(r1),
    .Carry(full_adder_2_carry));
  Full_Adder full_adder_3 (
    .Carry_in(full_adder_2_carry), .a_in(a2), .b_in(two_s_complement_1_out_11), .Result(r2),
    .Carry(full_adder_3_carry));
  Full_Adder full_adder_4 (
    .Carry_in(full_adder_3_carry), .a_in(a3), .b_in(two_s_complement_1_out_12), .Result(r3),
    .Carry(full_adder_4_carry));
  Full_Adder full_adder_5 (
    .Carry_in(full_adder_4_carry), .a_in(a4), .b_in(two_s_complement_1_out_13), .Result(r4),
    .Carry(full_adder_5_carry));
  Full_Adder full_adder_6 (
    .Carry_in(full_adder_5_carry), .a_in(a5), .b_in(two_s_complement_1_out_14), .Result(r5),
    .Carry(full_adder_6_carry));
  Full_Adder full_adder_7 (
    .Carry_in(full_adder_6_carry), .a_in(a6), .b_in(two_s_complement_1_out_15), .Result(r6),
    .Carry(full_adder_7_carry));
  Full_Adder full_adder_8 (
    .Carry_in(full_adder_7_carry), .a_in(a7), .b_in(two_s_complement_1_out_16), .Result(r7), .Carry(Overflow));

  // Notes on the sheet:
  //   Const 0
endmodule

module Quarter_Multiplier (
  input  [7:0] in_1,
  input  in_2,
  output [7:0] out_3,
  output [7:0] out_4,
  output out_5
);

  Shifter shifter_1 (.in(in_1), .\dist (3'b001), .out(out_3));
  and and_1 (out_4[0], in_2, in_1[0]);
  and and_2 (out_4[1], in_2, in_1[1]);
  and and_3 (out_4[2], in_2, in_1[2]);
  and and_4 (out_4[3], in_2, in_1[3]);
  and and_5 (out_4[4], in_2, in_1[4]);
  and and_6 (out_4[5], in_2, in_1[5]);
  and and_7 (out_4[6], in_2, in_1[6]);
  and and_8 (out_4[7], in_2, in_1[7]);

  assign out_5 = out_4[7];
endmodule

module Full_Multiplier (
  input  a0,
  input  a1,
  input  a2,
  input  a3,
  input  a4,
  input  a5,
  input  a6,
  input  a7,
  input  b0,
  input  b1,
  input  b2,
  input  b3,
  input  b4,
  input  b5,
  input  b6,
  input  b7,
  output r0,
  output r1,
  output r2,
  output r3,
  output r4,
  output r5,
  output r6,
  output r7
);

  wire [7:0] adder_8_bits_1_r0, adder_8_bits_2_r0, quarter_multiplier_1_out_3, quarter_multiplier_2_out_3,
       quarter_multiplier_3_out_3, quarter_multiplier_4_out_4;
  wire [7:1] quarter_multiplier_1_out_4, quarter_multiplier_2_out_4, quarter_multiplier_3_out_4;

  Quarter_Multiplier quarter_multiplier_1 (
    .in_1({b7, b6, b5, b4, b3, b2, b1, b0}), .in_2(a0), .out_3(quarter_multiplier_1_out_3),
    .out_4({quarter_multiplier_1_out_4, a1}));  // open: out_5
  Quarter_Multiplier quarter_multiplier_2 (
    .in_1(quarter_multiplier_1_out_3), .in_2(a1), .out_3(quarter_multiplier_2_out_3),
    .out_4({quarter_multiplier_2_out_4, a2}));  // open: out_5
  Adder_8_bits adder_8_bits_1 (
    .r0(adder_8_bits_1_r0[0]), .r1(adder_8_bits_1_r0[1]), .r2(adder_8_bits_1_r0[2]),
    .r3(adder_8_bits_1_r0[3]), .r4(adder_8_bits_1_r0[4]), .r5(adder_8_bits_1_r0[5]),
    .r6(adder_8_bits_1_r0[6]), .r7(adder_8_bits_1_r0[7]), .b0(a2), .b1(quarter_multiplier_2_out_4[1]),
    .b2(quarter_multiplier_2_out_4[2]), .b3(quarter_multiplier_2_out_4[3]),
    .b4(quarter_multiplier_2_out_4[4]), .b5(quarter_multiplier_2_out_4[5]),
    .b6(quarter_multiplier_2_out_4[6]), .b7(quarter_multiplier_2_out_4[7]), .a0(a1),
    .a1(quarter_multiplier_1_out_4[1]), .a2(quarter_multiplier_1_out_4[2]),
    .a3(quarter_multiplier_1_out_4[3]), .a4(quarter_multiplier_1_out_4[4]),
    .a5(quarter_multiplier_1_out_4[5]), .a6(quarter_multiplier_1_out_4[6]), .a7(quarter_multiplier_1_out_4[7]));  // open: Overflow
  Quarter_Multiplier quarter_multiplier_3 (
    .in_1(quarter_multiplier_2_out_3), .in_2(a2), .out_3(quarter_multiplier_3_out_3),
    .out_4({quarter_multiplier_3_out_4, a3}));  // open: out_5
  Quarter_Multiplier quarter_multiplier_4 (
    .in_1(quarter_multiplier_3_out_3), .in_2(a3), .out_4(quarter_multiplier_4_out_4));  // open: out_3, out_5
  Adder_8_bits adder_8_bits_2 (
    .r0(adder_8_bits_2_r0[0]), .r1(adder_8_bits_2_r0[1]), .r2(adder_8_bits_2_r0[2]),
    .r3(adder_8_bits_2_r0[3]), .r4(adder_8_bits_2_r0[4]), .r5(adder_8_bits_2_r0[5]),
    .r6(adder_8_bits_2_r0[6]), .r7(adder_8_bits_2_r0[7]), .b0(a3), .b1(quarter_multiplier_3_out_4[1]),
    .b2(quarter_multiplier_3_out_4[2]), .b3(quarter_multiplier_3_out_4[3]),
    .b4(quarter_multiplier_3_out_4[4]), .b5(quarter_multiplier_3_out_4[5]),
    .b6(quarter_multiplier_3_out_4[6]), .b7(quarter_multiplier_3_out_4[7]), .a0(adder_8_bits_1_r0[0]),
    .a1(adder_8_bits_1_r0[1]), .a2(adder_8_bits_1_r0[2]), .a3(adder_8_bits_1_r0[3]),
    .a4(adder_8_bits_1_r0[4]), .a5(adder_8_bits_1_r0[5]), .a6(adder_8_bits_1_r0[6]), .a7(adder_8_bits_1_r0[7]));  // open: Overflow
  Adder_8_bits adder_8_bits_3 (
    .r0(r0), .r1(r1), .r2(r2), .r3(r3), .r4(r4), .r5(r5), .r6(r6), .r7(r7),
    .b0(quarter_multiplier_4_out_4[0]), .b1(quarter_multiplier_4_out_4[1]),
    .b2(quarter_multiplier_4_out_4[2]), .b3(quarter_multiplier_4_out_4[3]),
    .b4(quarter_multiplier_4_out_4[4]), .b5(quarter_multiplier_4_out_4[5]),
    .b6(quarter_multiplier_4_out_4[6]), .b7(quarter_multiplier_4_out_4[7]), .a0(adder_8_bits_2_r0[0]),
    .a1(adder_8_bits_2_r0[1]), .a2(adder_8_bits_2_r0[2]), .a3(adder_8_bits_2_r0[3]),
    .a4(adder_8_bits_2_r0[4]), .a5(adder_8_bits_2_r0[5]), .a6(adder_8_bits_2_r0[6]), .a7(adder_8_bits_2_r0[7]));  // open: Overflow
  // Pins of 1 and 8 bits meet at {quarter_multiplier_3_out_4, a3}
  // Pins of 1 and 8 bits meet at {quarter_multiplier_1_out_4, a1}
  // Pins of 1 and 8 bits meet at {quarter_multiplier_2_out_4, a2}
endmodule

module Full_Multiplier_8 (
  input  a0,
  input  a1,
  input  a2,
  input  a3,
  input  a4,
  input  a5,
  input  a6,
  input  a7,
  input  b0,
  input  b1,
  input  b2,
  input  b3,
  input  b4,
  input  b5,
  input  b6,
  input  b7,
  output out_17,
  output out_18,
  output out_19,
  output out_20,
  output out_21,
  output out_22,
  output out_23,
  output out_24,
  output out_25,
  output out_26
);

  wire and_1_out, and_2_out, and_3_out, and_4_out, and_5_out, and_6_out, or_2_out, or_3_out, or_4_out,
       or_5_out, or_6_out, quarter_multiplier_1_out_5, quarter_multiplier_2_out_5,
       quarter_multiplier_3_out_5, quarter_multiplier_4_out_5, quarter_multiplier_5_out_5,
       quarter_multiplier_6_out_5, quarter_multiplier_7_out_5, quarter_multiplier_8_out_5;
  wire [7:0] m1, m2, m3, m4, m5, m6, quarter_multiplier_1_out_3, quarter_multiplier_2_out_3,
       quarter_multiplier_3_out_3, quarter_multiplier_4_out_3, quarter_multiplier_5_out_3,
       quarter_multiplier_6_out_3, quarter_multiplier_7_out_3, r0, r1, r2, r3, r4, r5, r6, r7;

  Quarter_Multiplier quarter_multiplier_1 (
    .in_1({b7, b6, b5, b4, b3, b2, b1, b0}), .in_2(a0), .out_3(quarter_multiplier_1_out_3), .out_4(r0),
    .out_5(quarter_multiplier_1_out_5));
  Quarter_Multiplier quarter_multiplier_2 (
    .in_1(quarter_multiplier_3_out_3), .in_2(a2), .out_3(quarter_multiplier_2_out_3), .out_4(r2),
    .out_5(quarter_multiplier_2_out_5));
  Quarter_Multiplier quarter_multiplier_3 (
    .in_1(quarter_multiplier_1_out_3), .in_2(a1), .out_3(quarter_multiplier_3_out_3), .out_4(r1),
    .out_5(quarter_multiplier_3_out_5));
  Quarter_Multiplier quarter_multiplier_4 (
    .in_1(quarter_multiplier_5_out_3), .in_2(a4), .out_3(quarter_multiplier_4_out_3), .out_4(r4),
    .out_5(quarter_multiplier_4_out_5));
  Quarter_Multiplier quarter_multiplier_5 (
    .in_1(quarter_multiplier_2_out_3), .in_2(a3), .out_3(quarter_multiplier_5_out_3), .out_4(r3),
    .out_5(quarter_multiplier_5_out_5));
  Quarter_Multiplier quarter_multiplier_6 (
    .in_1(quarter_multiplier_7_out_3), .in_2(a6), .out_3(quarter_multiplier_6_out_3), .out_4(r6),
    .out_5(quarter_multiplier_6_out_5));
  Quarter_Multiplier quarter_multiplier_7 (
    .in_1(quarter_multiplier_4_out_3), .in_2(a5), .out_3(quarter_multiplier_7_out_3), .out_4(r5),
    .out_5(quarter_multiplier_7_out_5));
  Adder_8_bits adder_8_bits_1 (
    .r0(m1[0]), .r1(m1[1]), .r2(m1[2]), .r3(m1[3]), .r4(m1[4]), .r5(m1[5]), .r6(m1[6]), .r7(m1[7]),
    .b0(r1[0]), .b1(r1[1]), .b2(r1[2]), .b3(r1[3]), .b4(r1[4]), .b5(r1[5]), .b6(r1[6]), .b7(r1[7]),
    .a0(r0[0]), .a1(r0[1]), .a2(r0[2]), .a3(r0[3]), .a4(r0[4]), .a5(r0[5]), .a6(r0[6]), .a7(r0[7]));  // open: Overflow
  Adder_8_bits adder_8_bits_2 (
    .r0(m6[0]), .r1(m6[1]), .r2(m6[2]), .r3(m6[3]), .r4(m6[4]), .r5(m6[5]), .r6(m6[6]), .r7(m6[7]),
    .b0(r6[0]), .b1(r6[1]), .b2(r6[2]), .b3(r6[3]), .b4(r6[4]), .b5(r6[5]), .b6(r6[6]), .b7(r6[7]),
    .a0(m5[0]), .a1(m5[1]), .a2(m5[2]), .a3(m5[3]), .a4(m5[4]), .a5(m5[5]), .a6(m5[6]), .a7(m5[7]));  // open: Overflow
  Quarter_Multiplier quarter_multiplier_8 (
    .in_1(quarter_multiplier_6_out_3), .in_2(a7), .out_4(r7), .out_5(quarter_multiplier_8_out_5));  // open: out_3
  or or_1 (out_26, quarter_multiplier_8_out_5, quarter_multiplier_6_out_5, quarter_multiplier_7_out_5, quarter_multiplier_4_out_5, quarter_multiplier_5_out_5, quarter_multiplier_2_out_5, quarter_multiplier_3_out_5, quarter_multiplier_1_out_5);
  Adder_8_bits adder_8_bits_3 (
    .r0(m2[0]), .r1(m2[1]), .r2(m2[2]), .r3(m2[3]), .r4(m2[4]), .r5(m2[5]), .r6(m2[6]), .r7(m2[7]),
    .b0(r2[0]), .b1(r2[1]), .b2(r2[2]), .b3(r2[3]), .b4(r2[4]), .b5(r2[5]), .b6(r2[6]), .b7(r2[7]),
    .a0(m1[0]), .a1(m1[1]), .a2(m1[2]), .a3(m1[3]), .a4(m1[4]), .a5(m1[5]), .a6(m1[6]), .a7(m1[7]));  // open: Overflow
  Adder_8_bits adder_8_bits_4 (
    .r0(out_17), .r1(out_18), .r2(out_19), .r3(out_20), .r4(out_21), .r5(out_22), .r6(out_23), .r7(out_25),
    .b0(r7[0]), .b1(r7[1]), .b2(r7[2]), .b3(r7[3]), .b4(r7[4]), .b5(r7[5]), .b6(r7[6]), .b7(r7[7]),
    .a0(m6[0]), .a1(m6[1]), .a2(m6[2]), .a3(m6[3]), .a4(m6[4]), .a5(m6[5]), .a6(m6[6]), .a7(m6[7]));  // open: Overflow
  Adder_8_bits adder_8_bits_5 (
    .r0(m3[0]), .r1(m3[1]), .r2(m3[2]), .r3(m3[3]), .r4(m3[4]), .r5(m3[5]), .r6(m3[6]), .r7(m3[7]),
    .b0(r3[0]), .b1(r3[1]), .b2(r3[2]), .b3(r3[3]), .b4(r3[4]), .b5(r3[5]), .b6(r3[6]), .b7(r3[7]),
    .a0(m2[0]), .a1(m2[1]), .a2(m2[2]), .a3(m2[3]), .a4(m2[4]), .a5(m2[5]), .a6(m2[6]), .a7(m2[7]));  // open: Overflow
  Adder_8_bits adder_8_bits_6 (
    .r0(m4[0]), .r1(m4[1]), .r2(m4[2]), .r3(m4[3]), .r4(m4[4]), .r5(m4[5]), .r6(m4[6]), .r7(m4[7]),
    .b0(r4[0]), .b1(r4[1]), .b2(r4[2]), .b3(r4[3]), .b4(r4[4]), .b5(r4[5]), .b6(r4[6]), .b7(r4[7]),
    .a0(m3[0]), .a1(m3[1]), .a2(m3[2]), .a3(m3[3]), .a4(m3[4]), .a5(m3[5]), .a6(m3[6]), .a7(m3[7]));  // open: Overflow
  Adder_8_bits adder_8_bits_7 (
    .r0(m5[0]), .r1(m5[1]), .r2(m5[2]), .r3(m5[3]), .r4(m5[4]), .r5(m5[5]), .r6(m5[6]), .r7(m5[7]),
    .b0(r5[0]), .b1(r5[1]), .b2(r5[2]), .b3(r5[3]), .b4(r5[4]), .b5(r5[5]), .b6(r5[6]), .b7(r5[7]),
    .a0(m4[0]), .a1(m4[1]), .a2(m4[2]), .a3(m4[3]), .a4(m4[4]), .a5(m4[5]), .a6(m4[6]), .a7(m4[7]));  // open: Overflow
  or or_2 (or_2_out, a2, a3, a4, a5, a5, a6);
  or or_3 (or_3_out, a1, a1, a2, a3, a4, a5, a6);
  or or_4 (or_4_out, a3, a3, a4, a5, a6);
  or or_5 (or_5_out, a4, a5, a6);
  or or_6 (or_6_out, a5, a6);
  and and_1 (and_1_out, or_2_out, b5);
  and and_2 (and_2_out, b1, a6);
  and and_3 (and_3_out, b6, or_3_out);
  and and_4 (and_4_out, b4, or_4_out);
  and and_5 (and_5_out, b3, or_5_out);
  and and_6 (and_6_out, b2, or_6_out);
  or or_7 (out_24, and_1_out, and_2_out, and_3_out, and_4_out, and_5_out, and_6_out);

  // Other names for the same wires on the sheet: m7[7:0] = {out_25, out_23, out_22, out_21, out_20, out_19, out_18, out_17}
endmodule

module Modulo (
  input  a0,
  input  a1,
  input  a2,
  input  a3,
  input  a4,
  input  a5,
  input  a6,
  input  a7,
  input  Flag,
  output out_10,
  output out_11,
  output out_12,
  output out_13,
  output out_14,
  output out_15,
  output out_16,
  output out_17
);

  wire xor0, xor1, xor2, xor3, xor4, xor5, xor6, xor7;

  xor xor_1 (xor0, a0, Flag);
  xor xor_2 (xor1, a1, Flag);
  xor xor_3 (xor2, a2, Flag);
  xor xor_4 (xor3, a3, Flag);
  Adder_8_bits adder_8_bits_1 (
    .r0(out_10), .r1(out_11), .r2(out_12), .r3(out_13), .r4(out_14), .r5(out_15), .r6(out_16), .r7(out_17),
    .b0(Flag), .b1(1'b0), .b2(1'b0), .b3(1'b0), .b4(1'b0), .b5(1'b0), .b6(1'b0), .b7(1'b0), .a0(xor0),
    .a1(xor1), .a2(xor2), .a3(xor3), .a4(xor4), .a5(xor5), .a6(xor6), .a7(xor7));  // open: Overflow
  xor xor_5 (xor4, a4, Flag);
  xor xor_6 (xor5, a5, Flag);
  xor xor_7 (xor6, a6, Flag);
  xor xor_8 (xor7, a7, Flag);
endmodule

module Megaboga_Multiplier (
  input  a0,
  input  a1,
  input  a2,
  input  a3,
  input  a4,
  input  a5,
  input  a6,
  input  a7,
  input  b0,
  input  b1,
  input  b2,
  input  b3,
  input  b4,
  input  b5,
  input  b6,
  input  b7,
  output out_17,
  output out_18,
  output out_19,
  output out_20,
  output out_21,
  output out_22,
  output out_23,
  output out_24
);

  wire Flag;
  wire [7:0] Mod1, Mod2, R1;

  Modulo Modulo (
    .a0(a0), .a1(a1), .a2(a2), .a3(a3), .a4(a4), .a5(a5), .a6(a6), .a7(a7), .Flag(a7), .out_10(Mod1[0]),
    .out_11(Mod1[1]), .out_12(Mod1[2]), .out_13(Mod1[3]), .out_14(Mod1[4]), .out_15(Mod1[5]),
    .out_16(Mod1[6]), .out_17(Mod1[7]));
  Modulo Modulo_2 (
    .a0(b0), .a1(b1), .a2(b2), .a3(b3), .a4(b4), .a5(b5), .a6(b6), .a7(b7), .Flag(b7), .out_10(Mod2[0]),
    .out_11(Mod2[1]), .out_12(Mod2[2]), .out_13(Mod2[3]), .out_14(Mod2[4]), .out_15(Mod2[5]),
    .out_16(Mod2[6]), .out_17(Mod2[7]));
  Full_Multiplier_8 full_multiplier_8_1 (
    .a0(Mod1[0]), .b0(Mod2[0]), .a1(Mod1[1]), .b1(Mod2[1]), .a2(Mod1[2]), .b2(Mod2[2]), .a3(Mod1[3]),
    .b3(Mod2[3]), .a4(Mod1[4]), .b4(Mod2[4]), .a5(Mod1[5]), .b5(Mod2[5]), .a6(Mod1[6]), .b6(Mod2[6]),
    .a7(Mod1[7]), .b7(Mod2[7]), .out_17(R1[0]), .out_18(R1[1]), .out_19(R1[2]), .out_20(R1[3]),
    .out_21(R1[4]), .out_22(R1[5]), .out_23(R1[6]), .out_25(R1[7]));  // open: out_26, out_24
  xor xor_1 (Flag, a7, b7);
  Modulo modulo_3 (
    .a0(R1[0]), .a1(R1[1]), .a2(R1[2]), .a3(R1[3]), .a4(R1[4]), .a5(R1[5]), .a6(R1[6]), .a7(R1[7]),
    .Flag(Flag), .out_10(out_17), .out_11(out_18), .out_12(out_19), .out_13(out_20), .out_14(out_21),
    .out_15(out_22), .out_16(out_23), .out_17(out_24));

  // Other names for the same wires on the sheet: Result[7:0] = {out_24, out_23, out_22, out_21, out_20, out_19, out_18, out_17}
endmodule

module \Divisão  (
  input  DIVIDENDO,
  input  in_2,
  input  in_3,
  input  in_4,
  input  in_5,
  input  in_6,
  input  in_7,
  input  in_8,
  input  in_9,
  input  in_10,
  input  in_11,
  input  in_12,
  input  in_13,
  input  in_14,
  input  in_15,
  input  in_16,
  output out_17,
  output out_18,
  output out_19,
  output out_20,
  output out_21,
  output out_22,
  output out_23,
  output out_24
);

  wire and_1_out, clock_1_out, not_1_out, not_2_out, or_1_out, or_2_out, undriven;
  wire [7:0] counter_1_q, multiplexer_1_out, register_1_q, subtraction_2_r0;

  or or_1 (or_1_out, counter_1_q[0], counter_1_q[1], counter_1_q[2], counter_1_q[3], counter_1_q[4], counter_1_q[5], counter_1_q[6], counter_1_q[7]);
  Multiplexer #(.width(8)) multiplexer_1 (
    .in0({in_8, in_7, in_6, in_5, in_4, in_3, in_2, DIVIDENDO}), .in1(subtraction_2_r0),
    .out(multiplexer_1_out), .sel(or_1_out), .en(not_1_out));
  not not_1 (not_1_out, register_1_q[7]);
  Subtraction subtraction_1 (
    .a0(counter_1_q[0]), .a1(counter_1_q[1]), .a2(counter_1_q[2]), .a3(counter_1_q[3]), .a4(counter_1_q[4]),
    .a5(counter_1_q[5]), .a6(counter_1_q[6]), .a7(counter_1_q[7]), .b0(1'b0), .b1(1'b1), .b2(1'b0),
    .b3(1'b0), .b4(1'b0), .b5(1'b0), .b6(1'b0), .b7(1'b0), .r0(out_17), .r1(out_18), .r2(out_19),
    .r3(out_20), .r4(out_21), .r5(out_22), .r6(out_23), .r7(out_24));  // open: Overflow
  Counter counter_1 (.Q(counter_1_q), .clk(and_1_out));  // open: load, D, count, carry, clr
  Register register_1 (.D(multiplexer_1_out), .en(undriven), .Q(register_1_q), .clk(and_1_out));  // open: clr
  and and_1 (and_1_out, not_2_out, or_2_out, clock_1_out);
  not not_2 (not_2_out, register_1_q[7]);
  Clock clock_1 (.out(clock_1_out));
  or or_2 (or_2_out, in_9, in_10, in_11, in_12, in_13, in_14, in_15, in_16);
  Subtraction subtraction_2 (
    .a0(register_1_q[0]), .a1(register_1_q[1]), .a2(register_1_q[2]), .a3(register_1_q[3]),
    .a4(register_1_q[4]), .a5(register_1_q[5]), .a6(register_1_q[6]), .a7(register_1_q[7]), .b0(in_9),
    .b1(in_10), .b2(in_11), .b3(in_12), .b4(in_13), .b5(in_14), .b6(in_15), .b7(in_16),
    .r0(subtraction_2_r0[0]), .r1(subtraction_2_r0[1]), .r2(subtraction_2_r0[2]), .r3(subtraction_2_r0[3]),
    .r4(subtraction_2_r0[4]), .r5(subtraction_2_r0[5]), .r6(subtraction_2_r0[6]), .r7(subtraction_2_r0[7]));  // open: Overflow

  // Notes on the sheet:
  //   DIVISOR
endmodule

module Megaboga_Divider (
  input  a0,
  input  a1,
  input  a2,
  input  a3,
  input  a4,
  input  a5,
  input  a6,
  input  a7,
  input  b0,
  input  b1,
  input  b2,
  input  b3,
  input  b4,
  input  b5,
  input  b6,
  input  b7,
  output out_17,
  output out_18,
  output out_19,
  output out_20,
  output out_21,
  output out_22,
  output out_23,
  output out_24
);

  wire Flag;
  wire [7:0] Mod1, Mod2, R1;

  Modulo Modulo (
    .a0(a0), .a1(a1), .a2(a2), .a3(a3), .a4(a4), .a5(a5), .a6(a6), .a7(a7), .Flag(a7), .out_10(Mod1[0]),
    .out_11(Mod1[1]), .out_12(Mod1[2]), .out_13(Mod1[3]), .out_14(Mod1[4]), .out_15(Mod1[5]),
    .out_16(Mod1[6]), .out_17(Mod1[7]));
  Modulo Modulo_2 (
    .a0(b0), .a1(b1), .a2(b2), .a3(b3), .a4(b4), .a5(b5), .a6(b6), .a7(b7), .Flag(b7), .out_10(Mod2[0]),
    .out_11(Mod2[1]), .out_12(Mod2[2]), .out_13(Mod2[3]), .out_14(Mod2[4]), .out_15(Mod2[5]),
    .out_16(Mod2[6]), .out_17(Mod2[7]));
  \Divisão  \divisão_1  (
    .DIVIDENDO(Mod1[0]), .in_2(Mod1[1]), .in_3(Mod1[2]), .in_4(Mod1[3]), .in_5(Mod1[4]), .in_6(Mod1[5]),
    .in_7(Mod1[6]), .in_8(Mod1[7]), .in_9(Mod2[0]), .in_10(Mod2[1]), .in_11(Mod2[2]), .in_12(Mod2[3]),
    .in_13(Mod2[4]), .in_14(Mod2[5]), .in_15(Mod2[6]), .in_16(Mod2[7]), .out_17(R1[0]), .out_18(R1[1]),
    .out_19(R1[2]), .out_20(R1[3]), .out_21(R1[4]), .out_22(R1[5]), .out_23(R1[6]), .out_24(R1[7]));
  xor xor_1 (Flag, a7, b7);
  Modulo modulo_3 (
    .a0(R1[0]), .a1(R1[1]), .a2(R1[2]), .a3(R1[3]), .a4(R1[4]), .a5(R1[5]), .a6(R1[6]), .a7(R1[7]),
    .Flag(Flag), .out_10(out_17), .out_11(out_18), .out_12(out_19), .out_13(out_20), .out_14(out_21),
    .out_15(out_22), .out_16(out_23), .out_17(out_24));

  // Other names for the same wires on the sheet: Result[7:0] = {out_24, out_23, out_22, out_21, out_20, out_19, out_18, out_17}
endmodule

module Resto (
  input  a0,
  input  a1,
  input  a2,
  input  a3,
  input  a4,
  input  a5,
  input  a6,
  input  a7,
  input  b0,
  input  b1,
  input  b2,
  input  b3,
  input  b4,
  input  b5,
  input  b6,
  input  b7,
  output out_17,
  output out_18,
  output out_19,
  output out_20,
  output out_21,
  output out_22,
  output out_23,
  output out_24
);

  wire megaboga_divider_1_out_17, megaboga_divider_1_out_18, megaboga_divider_1_out_19,
       megaboga_divider_1_out_20, megaboga_divider_1_out_21, megaboga_divider_1_out_22,
       megaboga_divider_1_out_23, megaboga_divider_1_out_24, megaboga_multiplier_1_out_17,
       megaboga_multiplier_1_out_18, megaboga_multiplier_1_out_19, megaboga_multiplier_1_out_20,
       megaboga_multiplier_1_out_21, megaboga_multiplier_1_out_22, megaboga_multiplier_1_out_23,
       megaboga_multiplier_1_out_24;

  Megaboga_Divider megaboga_divider_1 (
    .a0(a0), .a1(a1), .a2(a2), .a3(a3), .a4(a4), .a5(a5), .a6(a6), .a7(a7), .b0(b0), .b1(b1), .b2(b2),
    .b3(b3), .b4(b4), .b5(b5), .b6(b6), .b7(b7), .out_17(megaboga_divider_1_out_17),
    .out_18(megaboga_divider_1_out_18), .out_19(megaboga_divider_1_out_19),
    .out_20(megaboga_divider_1_out_20), .out_21(megaboga_divider_1_out_21),
    .out_22(megaboga_divider_1_out_22), .out_23(megaboga_divider_1_out_23), .out_24(megaboga_divider_1_out_24));
  Megaboga_Multiplier megaboga_multiplier_1 (
    .a0(megaboga_divider_1_out_17), .a1(megaboga_divider_1_out_18), .a2(megaboga_divider_1_out_19),
    .a3(megaboga_divider_1_out_20), .a4(megaboga_divider_1_out_21), .a5(megaboga_divider_1_out_22),
    .a6(megaboga_divider_1_out_23), .a7(megaboga_divider_1_out_24), .b0(b0), .b1(b1), .b2(b2), .b3(b3),
    .b4(b4), .b5(b5), .b6(b6), .b7(b7), .out_17(megaboga_multiplier_1_out_17),
    .out_18(megaboga_multiplier_1_out_18), .out_19(megaboga_multiplier_1_out_19),
    .out_20(megaboga_multiplier_1_out_20), .out_21(megaboga_multiplier_1_out_21),
    .out_22(megaboga_multiplier_1_out_22), .out_23(megaboga_multiplier_1_out_23),
    .out_24(megaboga_multiplier_1_out_24));
  Subtraction subtraction_1 (
    .a0(a0), .a1(a1), .a2(a2), .a3(a3), .a4(a4), .a5(a5), .a6(a6), .a7(a7),
    .b0(megaboga_multiplier_1_out_17), .b1(megaboga_multiplier_1_out_18), .b2(megaboga_multiplier_1_out_19),
    .b3(megaboga_multiplier_1_out_20), .b4(megaboga_multiplier_1_out_21), .b5(megaboga_multiplier_1_out_22),
    .b6(megaboga_multiplier_1_out_23), .b7(megaboga_multiplier_1_out_24), .r0(out_17), .r1(out_18),
    .r2(out_19), .r3(out_20), .r4(out_21), .r5(out_22), .r6(out_23), .r7(out_24));  // open: Overflow

  // Other names for the same wires on the sheet: Result[7:0] = {out_24, out_23, out_22, out_21, out_20, out_19, out_18, out_17}
endmodule
